# Fritzing sketch IR_decoder_Sketch (saved by Fritzing 0.8.7b)
breadboards: 1

parts:
  IR1 = TSOP312.., 314.. [package=THT]
  Part1 = Arduino Uno (Rev3) - ICSP

nets:
  N1: IR1.GND, Part1.D7
  N2: IR1.Vs, Part1.GND
  N3: IR1.Data, Part1.5V
