# Fritzing sketch servo_IR_Sketch (saved by Fritzing 0.8.7b)
breadboards: 1

parts:
  IR1 = TSOP312.., 314.. [package=THT]
  J1 = Basic Servo
  Part1 = Arduino Uno (Rev3) - ICSP

nets:
  N1: IR1.GND, Part1.ICSP_MOSI, Part1.D11_PWM/MOSI
  GND: IR1.Vs, J1.gnd, Part1.GND
  N2: IR1.Data, Part1.5V
  N3: J1.pulse, Part1.D9_PWM
