# Fritzing sketch jogodamemoria_Sketch (saved by Fritzing 0.8.7b)
breadboards: 1

parts:
  S2 = Pushbutton [package="[THT]"]
  S3 = Pushbutton [package="[THT]"]
  S4 = Pushbutton [package="[THT]"]
  S5 = Pushbutton [package="[THT]"]
  LED4 = LED - 5mm [color="Blue (430nm)" package="5 mm [THT]"]
  R8 = Resistor [tolerance=±5% resistance=220 package=THT]
  LED5 = LED - 5mm [color="Red (633nm)" package="5 mm [THT]"]
  R11 = Resistor [tolerance=±5% resistance=220 package=THT]
  R12 = Resistor [tolerance=±5% resistance=220 package=THT]
  R13 = Resistor [tolerance=±5% resistance=220 package=THT]
  R14 = Resistor [tolerance=±5% resistance=220 package=THT]
  R15 = Resistor [tolerance=±5% resistance=220 package=THT]
  R16 = Resistor [tolerance=±5% resistance=220 package=THT]
  R17 = Resistor [tolerance=±5% resistance=220 package=THT]
  LED6 = LED - 5mm [color="Green (555nm)" package="5 mm [THT]"]
  LED7 = LED - 5mm [color="Yellow (595nm)" package="5 mm [THT]"]
  Part1 = Arduino Uno (Rev3)
  J1 = Piezo Speaker

nets:
  N1: S2.Pin_1, S2.Pin_2, S4.Pin_1, S4.Pin_2, S5.Pin_1, S5.Pin_2, LED6.anode, Part1.D8, Part1.5V
  N2: S2.Pin_3, S2.Pin_4, R12.Pin_1, Part1.D5_PWM
  N3: S3.Pin_1, S3.Pin_2
  N4: S3.Pin_3, S3.Pin_4, R13.Pin_1, Part1.D4
  N5: S4.Pin_3, S4.Pin_4, R15.Pin_1, Part1.D3_PWM
  N6: S5.Pin_3, S5.Pin_4, R16.Pin_1, Part1.D2
  N7: LED4.cathode, R14.Pin_1
  N8: LED4.anode, Part1.D9_PWM
  N9: R8.Pin_0, R11.Pin_0, R12.Pin_0, R13.Pin_0, R14.Pin_0, R16.Pin_0, R17.Pin_0, Part1.GND, J1.pin1
  N10: R8.Pin_1, LED6.cathode
  N11: LED5.cathode, R11.Pin_1
  N12: R17.Pin_1, LED7.cathode
  N13: LED7.anode, Part1.D7
