# Fritzing sketch matrix_Sketch (saved by Fritzing 0.9.3b)

parts:
  Disp1 = LBT2088AH [part_number=LBT2088AH]
  Part1 = Arduino Uno (Rev3)

nets:
  N1: Disp1.pin1, Part1.D13/SCK
  N2: Disp1.pin2, Part1.D12/MISO
  N3: Disp1.pin_3, Part1.D11_PWM/MOSI
  N4: Disp1.pin_4, Part1.D10_PWM/SS
  N5: Disp1.pin_5, Part1.A2
  N6: Disp1.pin_6, Part1.A3
  N7: Disp1.pin_7, Part1.A4/SDA
  N8: Disp1.pin_8, Part1.A5/SCL
  N9: Disp1.pin_9, Part1.D2
  N10: Disp1.pin_10, Part1.D3_PWM
  N11: Disp1.pin_11, Part1.D4
  N12: Disp1.pin_12, Part1.D5_PWM
  N13: Disp1.pin_13, Part1.D6_PWM
  N14: Disp1.pin_14, Part1.D7
  N15: Disp1.pin_15, Part1.D8
  N16: Disp1.pin_16, Part1.D9_PWM
